# Fritzing sketch 3-2 (saved by Fritzing 0.9.3b)
breadboards: 1

parts:
  Raspberry_Pi_1 = Raspberry Pi 3 [part_number=RPI-3-V1.2]
  R1 = Resistor [tolerance=±5% resistance=1k package=THT]
  S1 = Pushbutton [package="[THT]"]

nets:
  N1: Raspberry_Pi_1.GPIO4, R1.Pin_0
  N2: Raspberry_Pi_1.GND, S1.Pin_1, S1.Pin_2
  N3: R1.Pin_1, S1.Pin_3, S1.Pin_4
