# Fritzing sketch 3-3 (saved by Fritzing 0.9.3b)
breadboards: 1
perfboards: 1

parts:
  S2 = Pushbutton [package="[THT]"]
  Raspberry_Pi_1 = Raspberry Pi 3 [part_number=RPI-3]
  S1 = Pushbutton [package="[THT]"]
  R3 = Resistor [tolerance=±5% resistance=330 package=THT]
  R1 = Resistor [tolerance=±5% resistance=330 package=THT]
  R4 = Resistor [tolerance=±5% resistance=330 package=THT]
  R2 = Resistor [tolerance=±5% resistance=330 package=THT]
  R6 = Resistor [tolerance=±5% resistance=1k package=THT]
  R5 = Resistor [tolerance=±5% resistance=1k package=THT]
  LED1 = LED - 5mm [color="Red (633nm)" package="5 mm [THT]"]
  LED2 = LED - 5mm [color="Red (633nm)" package="5 mm [THT]"]
  LED3 = LED - 5mm [color="Red (633nm)" package="5 mm [THT]"]
  LED4 = LED - 5mm [color="Red (633nm)" package="5 mm [THT]"]

nets (from the breadboard view):
  N1: S2.Pin_1, S2.Pin_2, Raspberry_Pi_1.GND, S1.Pin_1, S1.Pin_2, LED1.cathode, LED2.cathode, LED3.cathode, LED4.cathode
  N2: S2.Pin_3, S2.Pin_4, R6.Pin_0
  N3: Raspberry_Pi_1.GPIO4, R1.Pin_1
  N4: Raspberry_Pi_1.GPIO17, R2.Pin_1
  N5: Raspberry_Pi_1.GPIO27, R4.Pin_1
  N6: Raspberry_Pi_1.GPIO21, R6.Pin_1
  N7: Raspberry_Pi_1.GPIO20, R5.Pin_0
  N8: Raspberry_Pi_1.GPIO25, R3.Pin_0
  N9: S1.Pin_3, S1.Pin_4, R5.Pin_1
  N10: R2.Pin_0, LED2.anode
