# Fritzing sketch 3-4 (saved by Fritzing 0.9.3b)
breadboards: 1

parts:
  Raspberry_Pi_1 = Raspberry Pi 3 [part_number=RPI-3-V1.2]
  ステッピングモータ = X113647 Stepper Driver Board [part_number=駆動回路 package=board]
  MOTOR1 = 28BYJ-48 Stepper Motor [part_number=ステッピングモータ]
  DC12V_＿＿DCジャック = Power plug [part_number=DC12V]

nets:
  N1: Raspberry_Pi_1.GPIO6, ステッピングモータ.IN1
  N2: Raspberry_Pi_1.GPIO13, ステッピングモータ.IN2
  N3: Raspberry_Pi_1.GPIO19, ステッピングモータ.IN3
  N4: Raspberry_Pi_1.GPIO26, ステッピングモータ.IN4
  GND: Raspberry_Pi_1.GND, ステッピングモータ.GND, DC12V_＿＿DCジャック.GND
  N5: ステッピングモータ.+V, DC12V_＿＿DCジャック.VCC
  N6: ステッピングモータ.BLUE, MOTOR1.BLUE
  N7: ステッピングモータ.PINK, MOTOR1.PINK
  N8: ステッピングモータ.YELLOW, MOTOR1.YELLOW
  N9: ステッピングモータ.ORANGE, MOTOR1.ORANGE
  N10: ステッピングモータ.RED, MOTOR1.RED

custom parts:
  X113647 Stepper Driver Board: A common stepper motor driver board based on ULN2003APG darlington array
  28BYJ-48 Stepper Motor: 28BYJ-48 gear-reduction stepper motor (small)
