# Fritzing sketch 3-5 (saved by Fritzing 0.9.3b)
breadboards: 1

parts:
  Raspberry_Pi_1 = Raspberry Pi 3 [part_number=RPI-3-V1.2]
  ステッピングモータ1 = 28BYJ-48 Stepper Motor
  DC12V__DCジャック = Power plug [part_number=DC12V]
  ステッピングモータ2 = 28BYJ-48 Stepper Motor
  ステッピングモータ駆動回路2 = X113647 Stepper Driver Board [package=board]
  R2 = Resistor [tolerance=±5% resistance=1k package=THT]
  R1 = Resistor [tolerance=±5% resistance=1k package=THT]
  S1 = Pushbutton [package="[THT]"]
  S2 = Pushbutton [package="[THT]"]
  ステッピングモータ駆動回路1 = X113647 Stepper Driver Board [part_number=X113647 package=board]

nets:
  N1: Raspberry_Pi_1.GPIO4, Raspberry_Pi_1.GPIO27, R1.Pin_1
  N2: Raspberry_Pi_1.GPIO5, R2.Pin_1
  N3: Raspberry_Pi_1.GPIO6, ステッピングモータ駆動回路1.IN1
  N4: Raspberry_Pi_1.GPIO13, ステッピングモータ駆動回路1.IN2
  N5: Raspberry_Pi_1.GPIO19, ステッピングモータ駆動回路1.IN3
  N6: Raspberry_Pi_1.GPIO26, ステッピングモータ駆動回路1.IN4
  N7: Raspberry_Pi_1.GPIO21, ステッピングモータ駆動回路2.IN4
  N8: Raspberry_Pi_1.GPIO20, ステッピングモータ駆動回路2.IN3
  N9: Raspberry_Pi_1.GPIO16, ステッピングモータ駆動回路2.IN2
  GND: Raspberry_Pi_1.GND, DC12V__DCジャック.GND, ステッピングモータ駆動回路2.GND, S1.Pin_3, S1.Pin_4, S2.Pin_3, S2.Pin_4, ステッピングモータ駆動回路1.GND
  N10: Raspberry_Pi_1.GPIO12, ステッピングモータ駆動回路2.IN1
  N11: ステッピングモータ1.BLUE, ステッピングモータ駆動回路1.BLUE
  N12: ステッピングモータ1.PINK, ステッピングモータ駆動回路1.PINK
  N13: ステッピングモータ1.RED, ステッピングモータ駆動回路1.RED
  N14: ステッピングモータ1.ORANGE, ステッピングモータ駆動回路1.ORANGE
  N15: ステッピングモータ1.YELLOW, ステッピングモータ駆動回路1.YELLOW
  N16: DC12V__DCジャック.VCC, ステッピングモータ駆動回路2.+V, ステッピングモータ駆動回路1.+V
  N17: ステッピングモータ2.BLUE, ステッピングモータ駆動回路2.BLUE
  N18: ステッピングモータ2.PINK, ステッピングモータ駆動回路2.PINK
  N19: ステッピングモータ2.RED, ステッピングモータ駆動回路2.RED
  N20: ステッピングモータ2.ORANGE, ステッピングモータ駆動回路2.ORANGE
  N21: ステッピングモータ2.YELLOW, ステッピングモータ駆動回路2.YELLOW
  N22: R2.Pin_0, S2.Pin_1, S2.Pin_2
  N23: R1.Pin_0, S1.Pin_1, S1.Pin_2

custom parts:
  28BYJ-48 Stepper Motor: 28BYJ-48 gear-reduction stepper motor (small)
  X113647 Stepper Driver Board: A common stepper motor driver board based on ULN2003APG darlington array
