# Fritzing sketch 4 (saved by Fritzing 0.9.3b)
breadboards: 2

parts:
  Raspberry_Pi_1 = Raspberry Pi 3 [part_number=RPI-3-V1.2]
  ステッピングモータ駆動回路1 = X113647 Stepper Driver Board [part_number=X113647 package=board]
  ステッピングモータ1 = 28BYJ-48 Stepper Motor
  DC12V__DCジャック = Power plug [part_number=DC12V]
  ステッピングモータ2 = 28BYJ-48 Stepper Motor
  ステッピングモータ駆動回路2 = X113647 Stepper Driver Board [part_number=X113647 package=board]
  R2 = Resistor [tolerance=±5% resistance=1k package=THT]
  R1 = Resistor [tolerance=±5% resistance=1k package=THT]
  S1 = Pushbutton [package="[THT]"]
  S2 = Pushbutton [package="[THT]"]
  ステッピングモータ3 = 28BYJ-48 Stepper Motor
  ステッピングモータ駆動回路3 = X113647 Stepper Driver Board [part_number=X113647 package=board]
  R4 = Resistor [tolerance=±5% resistance=1k package=THT]
  R3 = Resistor [tolerance=±5% resistance=1k package=THT]
  S3 = Pushbutton [package="[THT]"]
  S4 = Pushbutton [package="[THT]"]

nets:
  N1: Raspberry_Pi_1.GPIO4, R1.Pin_1
  N2: Raspberry_Pi_1.GPIO17, R3.Pin_1
  N3: Raspberry_Pi_1.GPIO22, R4.Pin_1
  N4: Raspberry_Pi_1.GPIO5, R2.Pin_1
  N5: Raspberry_Pi_1.GPIO6, ステッピングモータ駆動回路1.IN1
  N6: Raspberry_Pi_1.GPIO13, ステッピングモータ駆動回路1.IN2
  N7: Raspberry_Pi_1.GPIO19, ステッピングモータ駆動回路1.IN3
  N8: Raspberry_Pi_1.GPIO26, ステッピングモータ駆動回路1.IN4
  N9: Raspberry_Pi_1.GPIO21, ステッピングモータ駆動回路2.IN4
  N10: Raspberry_Pi_1.GPIO20, ステッピングモータ駆動回路2.IN3
  N11: Raspberry_Pi_1.GPIO16, ステッピングモータ駆動回路2.IN2
  GND: Raspberry_Pi_1.GND, ステッピングモータ駆動回路1.GND, DC12V__DCジャック.GND, ステッピングモータ駆動回路2.GND, S1.Pin_3, S1.Pin_4, S2.Pin_3, S2.Pin_4, ステッピングモータ駆動回路3.GND, S3.Pin_3, S3.Pin_4, S4.Pin_3, S4.Pin_4
  N12: Raspberry_Pi_1.GPIO12, ステッピングモータ駆動回路2.IN1
  N13: Raspberry_Pi_1.GPIO25, ステッピングモータ駆動回路3.IN4
  N14: Raspberry_Pi_1.GPIO24, ステッピングモータ駆動回路3.IN3
  N15: Raspberry_Pi_1.GPIO23, ステッピングモータ駆動回路3.IN2
  N16: Raspberry_Pi_1.GPIO18, ステッピングモータ駆動回路3.IN1
  N17: ステッピングモータ駆動回路1.+V, DC12V__DCジャック.VCC, ステッピングモータ駆動回路2.+V, ステッピングモータ駆動回路3.+V
  N18: ステッピングモータ駆動回路1.BLUE, ステッピングモータ1.BLUE
  N19: ステッピングモータ駆動回路1.PINK, ステッピングモータ1.PINK
  N20: ステッピングモータ駆動回路1.YELLOW, ステッピングモータ1.YELLOW
  N21: ステッピングモータ駆動回路1.ORANGE, ステッピングモータ1.ORANGE
  N22: ステッピングモータ駆動回路1.RED, ステッピングモータ1.RED
  N23: ステッピングモータ2.BLUE, ステッピングモータ駆動回路2.BLUE
  N24: ステッピングモータ2.PINK, ステッピングモータ駆動回路2.PINK
  N25: ステッピングモータ2.RED, ステッピングモータ駆動回路2.RED
  N26: ステッピングモータ2.ORANGE, ステッピングモータ駆動回路2.ORANGE
  N27: ステッピングモータ2.YELLOW, ステッピングモータ駆動回路2.YELLOW
  N28: R2.Pin_0, S2.Pin_1, S2.Pin_2
  N29: R1.Pin_0, S1.Pin_1, S1.Pin_2
  N30: ステッピングモータ3.BLUE, ステッピングモータ駆動回路3.BLUE
  N31: ステッピングモータ3.PINK, ステッピングモータ駆動回路3.PINK
  N32: ステッピングモータ3.RED, ステッピングモータ駆動回路3.RED
  N33: ステッピングモータ3.ORANGE, ステッピングモータ駆動回路3.ORANGE
  N34: ステッピングモータ3.YELLOW, ステッピングモータ駆動回路3.YELLOW
  N35: R4.Pin_0, S4.Pin_1, S4.Pin_2
  N36: R3.Pin_0, S3.Pin_1, S3.Pin_2

custom parts:
  X113647 Stepper Driver Board: A common stepper motor driver board based on ULN2003APG darlington array
  28BYJ-48 Stepper Motor: 28BYJ-48 gear-reduction stepper motor (small)
